# Fritzing sketch Base (saved by Fritzing 0.9.3b)
breadboards: 1

parts:
  Part1 = Arduino Uno (Rev3)
  LED1 = RGB LED (com. anode, rbg) [package="5 mm [THT]"]
  LED2 = RGB LED (com. anode, rbg) [package="5 mm [THT]"]
  LED3 = RGB LED (com. anode, rbg) [package="5 mm [THT]"]
  LED4 = RGB LED (com. anode, rbg) [package="5 mm [THT]"]
  J1 = Piezo Speaker
  S4 = Taiway 100-SP-X-T1 SPDT Miniature Toggle Switch [part_number=100-SP-X-T1-0-0-B1-M1 package=THT]
  S6 = SPST Switch [package=switch-spdt_lock.007s]

nets:
  N1: Part1.D2, LED2.green_cathode
  N2: Part1.D3_PWM, S6.S
  N3: Part1.D4, S4.L2
  N4: Part1.D5_PWM, S4.L1
  N5: Part1.D6_PWM, J1.pin2
  N6: Part1.5V, LED1.blue_cathode, LED2.blue_cathode, LED3.blue_cathode, LED4.blue_cathode, S4.COM
  N7: Part1.GND, LED1.common_anode, LED2.common_anode, LED3.common_anode, LED4.common_anode, J1.pin1, S6.O, S6.P
  N8: LED1.red_cathode, LED3.green_cathode
  N9: LED1.green_cathode, LED2.red_cathode
  N10: LED3.red_cathode, LED4.green_cathode
