# Fritzing sketch Semaforo (saved by Fritzing 0.9.3b)
breadboards: 1

parts:
  Part1 = Arduino Uno (Rev3)
  Part2 = LED Matrix - Serial Interface - Red/Green/Blue
  Part4 = LED Matrix - Serial Interface - Red/Green/Blue
  Part3 = LED Matrix - Serial Interface - Red/Green/Blue

nets:
  N1: Part1.D8, Part4.MOSI
  GND: Part1.D2, Part1.D3_PWM, Part1.GND, Part2.GND, Part4.GND, Part3.GND
  N2: Part1.D6_PWM, Part2.MOSI
  N3: Part1.D7, Part3.MOSI
  VCC: Part1.5V, Part2.VCC, Part4.VCC, Part3.VCC
